# Fritzing sketch prototype (saved by Fritzing 0.9.10b)
breadboards: 1

parts:
  Mod1 = Amica NodeMCU DEVKIT 1.0
  DHT11 = DHT11 Humitidy and Temperature Sensor
  TDS_Sensor = PH meter with sensor in breadboard [package=THT]
  BB_PWR1 = Toaster Bread Board Dual Supply [package="DIP (Dual Inline) [THT]"]
  R1 = Resistor [tolerance=±5% power=0.25 resistance=1k package=THT]

nets:
  N1: Mod1.pin1, Mod1.pin_10, Mod1.pin_26, DHT11.VDD, BB_PWR1.VS2, R1.Pin_1
  GND: Mod1.pin2, Mod1.pin_9, Mod1.pin_25, Mod1.pin_29, DHT11.GND, TDS_Sensor.pin3, BB_PWR1.GND
  N2: Mod1.pin_15, DHT11.DATA, R1.Pin_0
  N3: Mod1.pin_16, TDS_Sensor.pin1
  N4: TDS_Sensor.pin2, BB_PWR1.VS1

custom parts:
  DHT11 Humitidy and Temperature Sensor: DHT11 Humidity and Temperature Sensor
  PH meter with sensor in breadboard: DFrobot PH meter (SKU SEN0161)
  Toaster Bread Board Dual Supply: Toaster is dual output USB step up power supply module designed to fit snuggly into a breadboard. It is powered by a single 5V USB port or charger and outputs three voltages simultaneously, these being 3.3V, 5V and a variable supply which is capable of 5V to 16V.
